# Fritzing sketch CAN_Arduino_setup (saved by Fritzing 1.0.1rc)
breadboards: 2

parts:
  Part1 = Arduino Uno (Rev3) - ICSP
  M1 = Niren can bus module [package=THT]

nets:
  N1: Part1.ICSP_MOSI, Part1.D11_PWM/MOSI, M1.pin5
  N2: Part1.D10_PWM/SS, M1.pin3
  N3: Part1.D12/MISO, M1.pin4
  N4: Part1.D13/SCK, M1.pin6
  N5: Part1.D2, M1.pin7
  N6: Part1.GND, M1.pin2
  N7: Part1.VIN, M1.pin1
  N8: M1.pin10, M1.pin11, M1.pin12, M1.pin13

notes:
  Represents GX4875-2E controller
  CAN_H - CAN_L - GND
  <---- Has been connected!

custom parts:
  Niren can bus module: Niren can bus module availabe on ebay and others. Pcb view assumes that you unsolder the 7 pin header and resolder it on the bottom of the module to connect to the pcb. The two jumpers and the can bus connector remain on the top of the board and don't appear in pcb view.
