# Fritzing sketch PWM_Arduino_setup (saved by Fritzing 1.0.1rc)
breadboards: 1

parts:
  Mod1 = KY-023 Dual Axis Joystick Module [package="Breakout board"]
  Part1 = Arduino Uno (Rev3) - ICSP

nets:
  GND: Mod1.GND, Part1.GND
  +5V: Mod1.+5V, Part1.5V
  N1: Mod1.VRx, Part1.A0
  N2: Mod1.VRy, Part1.A1
  N3: Mod1.SW, Part1.D6_PWM

notes:
  Represents the GX4875-2E controller
  AIN1 - GND - AIN2

custom parts:
  KY-023 Dual Axis Joystick Module: KY-023 Dual-Axis Joystick Module.
